# Fritzing sketch whitecane v2 (saved by Fritzing 0.9.2b)
breadboards: 1

parts:
  Part1 = PowerBoost 500 Charger
  Teensy_3_1 = Teensy 3.1
  U1 = SWITCH_SPDT [package=kps-1290]
  C1 = Electrolytic Capacitor [capacitance=1000μF package="1010 [SMD, electrolytic]"]
  C2 = Electrolytic Capacitor [capacitance=1000μF package="1010 [SMD, electrolytic]"]
  MOTOR1 = Vibration Motor
  D1 = Rectifier Diode [part_number=1N4001 package="300 mil [THT]"]
  Part2 = SRF05 Ultrasonic Rangefinder
  MOTOR2 = Vibration Motor

nets:
  N1: Part1.ENABLE, U1.O
  N2: Part1.GND, U1.P
  N3: Part1.LBO, U1.S
  N4: Part1.5.0V, C1.+, C2.+, D1.cathode, Part2.VCC
  N5: Teensy_3_1.D0, MOTOR2.POS
  N6: Teensy_3_1.D1, MOTOR1.POS
  N7: C1.-, C2.-, MOTOR1.NEG, Part2.GND, MOTOR2.NEG

custom parts:
  PowerBoost 500 Charger: The PowerBoost 500C is a little DC/DC boost converter module that can be powered by any 3.7V LiIon/LiPoly battery, and convert the battery output to 5.2V DC for running your 5V projects. At its heart is a TPS61090 boost converter from TI. This boost converter chip has some really nice extras such as low battery detection, 2A internal switch, synchronous conversion, excellent efficiency, and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
  Vibration Motor: An eccentric vibration motor!
