# Fritzing sketch whitecane (saved by Fritzing 0.9.2b)
breadboards: 1

parts:
  Part1 = PowerBoost 500 Charger
  Teensy_3_1 = Teensy 3.1  # not connected
  U1 = SWITCH_SPDT [package=kps-1290]
  C1 = Electrolytic Capacitor [capacitance=1000μF package="1010 [SMD, electrolytic]"]
  C2 = Electrolytic Capacitor [capacitance=1000μF package="1010 [SMD, electrolytic]"]
  Q1 = Basic FET N-Channel [package="D2Pak [SMD]"]
  R2 = Resistor [tolerance=±5% resistance=320 package=THT]
  MOTOR1 = Vibration Motor
  D1 = Rectifier Diode [part_number=1N4001 package="300 mil [THT]"]
  D2 = Rectifier Diode [part_number=1N4001 package="300 mil [THT]"]
  Part2 = SRF05 Ultrasonic Rangefinder

nets:
  N1: Part1.ENABLE, U1.O
  N2: Part1.GND, U1.P
  N3: Part1.LBO, U1.S
  N4: Part1.5.0V, C1.-, C2.-, Q1.source, Part2.GND
  N5: C1.+, R2.Pin_1, MOTOR1.POS, D2.cathode
  N6: C2.+, R2.Pin_0, D1.cathode, Part2.VCC
  N7: Q1.drain, MOTOR1.NEG, D2.anode

custom parts:
  PowerBoost 500 Charger: The PowerBoost 500C is a little DC/DC boost converter module that can be powered by any 3.7V LiIon/LiPoly battery, and convert the battery output to 5.2V DC for running your 5V projects. At its heart is a TPS61090 boost converter from TI. This boost converter chip has some really nice extras such as low battery detection, 2A internal switch, synchronous conversion, excellent efficiency, and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
  Vibration Motor: An eccentric vibration motor!
